# Fritzing sketch Egg (saved by Fritzing 0.9.3b)
breadboards: 1

parts:
  U1 = ESP8266 NodeMCU LoLin module
  hc-sr1 = hc-sr04

nets:
  N1: U1.D1, hc-sr1.Trig
  N2: U1.D2, hc-sr1.Echo
  VIN: U1.Vin, hc-sr1.VCC
  GND: U1.GND, hc-sr1.GND

notes:
  18BCE0018
  Ultra Sonic - VCC to Vin , GND to GND, Echo to D2,
  Trig to D1

custom parts:
  ESP8266 NodeMCU LoLin module: ESP8266 based NodeMCU
