# Fritzing sketch Final (saved by Fritzing 0.9.3b)
breadboards: 1

parts:
  U1 = ESP8266 NodeMCU LoLin module
  hc-sr1 = hc-sr04
  U2 = GAS_SENSOR [package=mq-3]
  IR1 = TSOP312.., 314.. [package=THT]

nets:
  N1: U1.D1, hc-sr1.Trig
  N2: U1.D2, hc-sr1.Echo
  N3: U1.D4, IR1.Data
  GND: U1.GND, hc-sr1.GND, U2.H1, IR1.GND
  VIN: U1.Vin, hc-sr1.VCC, U2.H2, IR1.Vs
  N4: U1.A0, U2.A1

notes:
  18BCE0018

custom parts:
  ESP8266 NodeMCU LoLin module: ESP8266 based NodeMCU
