# Fritzing sketch Gas (saved by Fritzing 0.9.3b)
breadboards: 1

parts:
  U1 = ESP8266 NodeMCU LoLin module
  U2 = GAS_SENSOR [package=mq-3]

nets:
  N1: U1.Vin, U2.H2
  N2: U1.GND, U2.H1
  N3: U1.A0, U2.B1, U2.A1

notes:
  18BCE0018
  MQ2 Gas Sensor - VCC to Vin , GND to GND,
  A0 to A0;

custom parts:
  ESP8266 NodeMCU LoLin module: ESP8266 based NodeMCU
