# Fritzing sketch IR (saved by Fritzing 0.9.3b)
breadboards: 1

parts:
  U1 = ESP8266 NodeMCU LoLin module
  IR1 = TSOP312.., 314.. [package=THT]

nets:
  N1: U1.D4, IR1.Data
  GND: U1.GND, IR1.GND
  N2: U1.Vin, IR1.Vs

notes:
  18BCE0018
  Infrared - VCC to Vin , GND to GND , Out to D4

custom parts:
  ESP8266 NodeMCU LoLin module: ESP8266 based NodeMCU
